// Logisim project counter-halt-65535.circ as structural Verilog: 1 circuit, main circuit main
module main (
  output [15:0] Q,
  output halt
);

  wire clock_1_out;

  Clock clock_1 (.out(clock_1_out));
  Counter #(.width(16), .max('hffff)) counter_1 ();  // open: load, D, count, Q, carry, clk, clr
  Comparator #(.width(16)) comparator_1 (.a(Q), .b({16{1'b1}}), .eq(halt));  // open: gt, lt
endmodule
