// Logisim project full-adder-v5.circ as structural Verilog: 1 circuit, main circuit main
module main (
  input  A,
  input  B,
  input  Cin,
  output S,
  output Cout
);

  wire N1, N2, X1;

  xor xor_1 (X1, A, B);
  xor xor_2 (S, X1, Cin);
  and and_1 (N1, A, B);
  and and_2 (N2, X1, Cin);
  or or_1 (Cout, N1, N2);
endmodule
