// Logisim project rom-seq.circ as structural Verilog: 1 circuit, main circuit main
module main (
  output [7:0] D,
  output halt
);

  wire clock_1_out;
  wire [3:0] counter_1_q;

  Clock clock_1 (.out(clock_1_out));
  Counter #(.width(4), .max('hf)) counter_1 (
    .clk(clock_1_out), .Q(counter_1_q));  // open: clr, load, up, count, D, carry
  ROM #(.addrWidth(4), .dataWidth(8)) PROG (.addr(counter_1_q), .data(D));
  Comparator #(.width(4)) comparator_1 (.a(counter_1_q), .b(4'b1111), .eq(halt));  // open: gt, lt
endmodule
