// Logisim project wire-colours-no-width-v5.circ as structural Verilog: 1 circuit, main circuit main
module main (
  output OK,
  output E,
  output X
);


  assign E = 1'b0;
  assign OK = 1'b1;

  // Notes on the sheet:
  //   1: normal (1 = bright green)
  //   2: two drivers disagree (E, red)
  //   3: nothing drives the wire (X, blue)
endmodule
