// Logisim project wire-colours-v5.circ as structural Verilog: 1 circuit, main circuit main
module main (
  input  [3:0] D,
  output OK,
  output E,
  output X,
  output W
);

  // Pins of 1 and 4 bits meet at D

  assign E = 1'b0;
  assign OK = 1'b1;
  assign W = D[0];

  // Notes on the sheet:
  //   1: normal (1 = bright green)
  //   2: two drivers disagree (E, red)
  //   3: nothing drives the wire (X, blue)
  //   4: 4-bit wire into 1-bit pin (orange)
endmodule
